# Fritzing sketch bahn (saved by Fritzing 0.9.3b)
circuit board: 8.46667cm x 5.64444cm

parts:
  WeMos_D1_Mini1 = WeMos D1 Mini
  Lok_-_Motor = DC Motor  # not connected
  Part3 = RFID-RC522-v2
  470uf = Electrolytic Capacitor [capacitance=100nF voltage=35V package="0405 [SMD, electrolytic]"]
  IRL3803 = Basic FET N-Channel [package="TO220 [THT]"]
  R2 = Resistor [tolerance=±5% resistance=220 package=THT]
  Step_Down_-_LM2596DC = Voltage Regulator LM1117 [package=sot223]
  hc-sr1_-_Ultraschallsensor = hc-sr04
  U1 = 2-Channel 5v Relay Shield [package=relay-2ch5v10a]
  Gleis_/_Lok = Power Jack [package=power_jack_slot]
  D1 = Rectifier Diode [part_number=1N4001 package="Melf DO-213 AB [SMD]"]  # not connected
  C1 = Tantalum Capacitor [capacitance=1μF package="100 mil [THT, tantalum]"]

nets:
  N1: WeMos_D1_Mini1.3V3, Part3.3_3V
  5V: WeMos_D1_Mini1.5V, U1.VCC
  N2: WeMos_D1_Mini1.D0, Part3.RST
  N3: WeMos_D1_Mini1.D2, hc-sr1_-_Ultraschallsensor.Echo
  N4: WeMos_D1_Mini1.D3, R2.Pin_0
  N5: WeMos_D1_Mini1.D4, hc-sr1_-_Ultraschallsensor.Trig
  N6: WeMos_D1_Mini1.D5, Part3.SCK
  N7: WeMos_D1_Mini1.D6, Part3.MISO
  N8: WeMos_D1_Mini1.D7, Part3.MOSI
  N9: WeMos_D1_Mini1.D8, Part3.SDA
  N10: WeMos_D1_Mini1.G, U1.GND
  N11: 470uf.-, C1.-
  N12: IRL3803.gate, R2.Pin_1
  N13: Step_Down_-_LM2596DC.ADJ, Gleis_/_Lok.GNDBREAK
  N14: Step_Down_-_LM2596DC.OUT, Gleis_/_Lok.PWR
  N15: U1.IN1, U1.IN2

notes:
  5V
  12 - 18 V
  3,3V
  Steuerung Eisenbahn - LOK
  07.09.2017
  .

custom parts:
  RFID-RC522-v2: A simple China made RFID-RC522 Reader; do check the pin labels, as this is a MFRC522 based clone.
  2-Channel 5v Relay Shield: 2 Channel 5v Relay Shield w. 2x SPD-06VDC-SD-C
